// Digital circuit 1Bit_FDE_Cycle.dig as structural Verilog
module _1Bit_FDE_Cycle (
  input  In,
  input  K,
  output B_plus_1,
  output A_plus_1
);

  wire and_1_out, and_2_out, and_3_out, and_4_out, not_1_out, not_2_out, not_3_out, not_4_out, not_5_out,
       not_6_out, not_7_out, or_1_out, or_2_out;

  not not_1 (not_1_out, B_plus_1);
  not not_2 (not_2_out, In);
  not not_3 (not_3_out, A_plus_1);
  not not_4 (not_4_out, A_plus_1);
  not not_5 (not_5_out, B_plus_1);
  not not_6 (not_6_out, A_plus_1);
  not not_7 (not_7_out, In);
  and and_1 (and_1_out, A_plus_1, not_1_out, not_2_out);
  and and_2 (and_2_out, not_3_out, B_plus_1, In);
  and and_3 (and_3_out, not_4_out, not_5_out, In);
  and and_4 (and_4_out, not_6_out, B_plus_1, not_7_out);
  or or_1 (or_1_out, and_1_out, and_2_out);
  or or_2 (or_2_out, and_3_out, and_4_out);
  D_FF d_ff_1 (.D(or_1_out), .C(K), .Q(A_plus_1));  // open: nQ
  D_FF d_ff_2 (.D(or_2_out), .C(K), .Q(B_plus_1));  // open: nQ
endmodule
