// Digital circuit 4Bit_ALU.dig as structural Verilog
module _4Bit_ALU (
  input  [3:0] A,
  input  [3:0] B,
  input  [2:0] Cin,
  output [3:0] Cout,
  output Z
);

  wire _4bit_full_adder_1_p5, _4bit_subtractor_1_p5;
  wire [0:0] _4bit_slt_1_p3;
  wire [3:0] _4bit_full_adder_1_p4, _4bit_subtractor_1_p4, and_1_out, or_1_out, xor_1_out;

  // _4Bit_Full_Adder _4bit_full_adder_1: pin names not known; wires that end beside it: B, A, 1'b0, _4bit_full_adder_1_p4, _4bit_full_adder_1_p5
  // _4Bit_Subtractor _4bit_subtractor_1: pin names not known; wires that end beside it: A, B, 1'b1, _4bit_subtractor_1_p4, _4bit_subtractor_1_p5
  assign and_1_out = A & B;  // And and_1, 4 bits wide
  assign or_1_out = A | B;  // Or or_1, 4 bits wide
  assign xor_1_out = A ^ B;  // XOr xor_1, 4 bits wide
  // _4Bit_SLT _4bit_slt_1: pin names not known; wires that end beside it: A, B, _4bit_slt_1_p3[0]
  LED led_1 (.in(_4bit_full_adder_1_p5));
  LED led_2 (.in(_4bit_subtractor_1_p5));
  Multiplexer #(.Selector_Bits(3), .Bits(4)) multiplexer_1 (
    .sel(Cin), .in_0(_4bit_full_adder_1_p4), .in_1(_4bit_subtractor_1_p4), .in_2(and_1_out), .in_3(or_1_out),
    .in_4(xor_1_out), .in_5({3'b001, _4bit_slt_1_p3[0]}), .in_6(A), .in_7(B), .out(Cout));
  nor nor_1 (Z, Cout[0], Cout[1], Cout[2], Cout[3]);
endmodule
