// Digital circuit 4Bit_CPU.dig as structural Verilog
module _4Bit_CPU (
  input  clk,
  input  Cin
);

  wire _4bit_alu_1_p1, _4bit_alu_1_p2, _4bit_alu_1_p3, _4bit_alu_1_p4, _4bit_alu_1_p5, _4bit_cu_1_p1,
       _4bit_cu_1_p2, _4bit_cu_1_p3, _4bit_cu_1_p4, _4bit_cu_1_p8, _4bit_cu_1_p9, _4bit_cu_1_p10,
       _4bit_cu_1_p11, _4bit_cu_1_p12, _4bit_cu_1_p13, _4bit_cu_1_p14, _4bit_ram_module_1_p2,
       _4bit_ram_module_1_p3, _4bit_ram_module_1_p4, _4bit_register_file_1_p4, _4bit_register_file_1_p6,
       _4bit_register_file_1_p7, _4bit_register_file_1_p8, _4bit_register_file_1_p9, IP_p3, IP_p4, IP_p5,
       IP_p6, IR_p1, IR_p3, IR_p4, notconnected_8_out, notconnected_9_out, notconnected_10_out,
       notconnected_11_out, notconnected_12_out, notconnected_13_out;

  // _4Bit_Register IP: pin names not known; wires that end beside it: Cin, clk, IP_p3, IP_p4, IP_p5, IP_p6
  // NotConnected on IP_p3
  // NotConnected on IP_p4
  // NotConnected on IP_p5
  // NotConnected on IP_p6
  // _4Bit_Register IR: pin names not known; wires that end beside it: IR_p1, clk, IR_p3, IR_p4
  // NotConnected on IR_p1
  // NotConnected on IR_p3
  // NotConnected on IR_p4
  // NotConnected on notconnected_8_out
  // NotConnected on notconnected_9_out
  // NotConnected on notconnected_10_out
  // NotConnected on notconnected_11_out
  // NotConnected on notconnected_12_out
  // NotConnected on notconnected_13_out
  // _4Bit_CU _4bit_cu_1: pin names not known; wires that end beside it: _4bit_cu_1_p1, _4bit_cu_1_p2, _4bit_cu_1_p3, _4bit_cu_1_p4, notconnected_8_out, notconnected_9_out, clk, _4bit_cu_1_p8, _4bit_cu_1_p9, _4bit_cu_1_p10, _4bit_cu_1_p11, _4bit_cu_1_p12, _4bit_cu_1_p13, _4bit_cu_1_p14
  // _4Bit_Program_Counter _4bit_program_counter_1: pin names not known; wires that end beside it: notconnected_10_out, notconnected_11_out, clk, notconnected_12_out, notconnected_13_out
  // NotConnected on _4bit_cu_1_p12
  // NotConnected on _4bit_cu_1_p13
  // NotConnected on _4bit_cu_1_p14
  // _4Bit_Register_File _4bit_register_file_1: pin names not known; wires that end beside it: _4bit_cu_1_p8, _4bit_cu_1_p9, _4bit_cu_1_p10, _4bit_register_file_1_p4, _4bit_cu_1_p11, _4bit_register_file_1_p6, _4bit_register_file_1_p7, _4bit_register_file_1_p8, _4bit_register_file_1_p9
  // NotConnected on _4bit_register_file_1_p4
  // NotConnected on _4bit_register_file_1_p6
  // NotConnected on _4bit_register_file_1_p7
  // NotConnected on _4bit_register_file_1_p8
  // NotConnected on _4bit_register_file_1_p9
  // _4Bit_ALU _4bit_alu_1: pin names not known; wires that end beside it: _4bit_alu_1_p1, _4bit_alu_1_p2, _4bit_alu_1_p3, _4bit_alu_1_p4, _4bit_alu_1_p5
  // NotConnected on _4bit_alu_1_p1
  // NotConnected on _4bit_alu_1_p2
  // NotConnected on _4bit_alu_1_p3
  // _4Bit_Ram_Module _4bit_ram_module_1: pin names not known; wires that end beside it: clk, _4bit_ram_module_1_p2, _4bit_ram_module_1_p3, _4bit_ram_module_1_p4
  // NotConnected on _4bit_ram_module_1_p2
  // NotConnected on _4bit_ram_module_1_p3
  // NotConnected on _4bit_alu_1_p4
  // NotConnected on _4bit_alu_1_p5
  // NotConnected on _4bit_ram_module_1_p4
endmodule
