// Digital circuit 4Bit_CU.dig as structural Verilog
module _4Bit_CU (
  input  A,
  input  B,
  input  C,
  input  D,
  input  R,
  input  Z,
  input  K,
  output RR1,
  output RR2,
  output WR,
  output WE,
  output IL,
  output [2:0] ALU,
  output PCI,
  output IFE
);

  wire _1bit_fde_cycle_1_a_plus_1, _1bit_fde_cycle_1_b_plus_1, notconnected_3_out;

  // NotConnected on R
  // NotConnected on Z
  RR1_Opcode rr1_opcode_1 (.A(A), .B(B), .C(C), .D(D), .RR1(RR1));
  RR2_Opcode rr2_opcode_1 (.A(A), .B(B), .C(C), .D(D), .RR2(RR2));
  WR_Opcode wr_opcode_1 (.A(A), .B(B), .C(C), .D(D), .WR(WR));
  WE_Opcode we_opcode_1 (.A(A), .C(C), .D(D), .WE(WE));
  IL_Opcode il_opcode_1 (.A(A), .C(C), .D(D), .IL(IL));
  _4Bit_CU_ALU_Master_Mapper _4bit_cu_alu_master_mapper_1 (.A(A), .B(B), .C(C), .D(D), .ALU(ALU));
  _1Bit_FDE_Cycle _1bit_fde_cycle_1 (
    .In(notconnected_3_out), .K(K), .B_plus_1(_1bit_fde_cycle_1_b_plus_1),
    .A_plus_1(_1bit_fde_cycle_1_a_plus_1));
  // NotConnected on notconnected_3_out
  LED led_1 (.in(_1bit_fde_cycle_1_b_plus_1));
  LED led_2 (.in(_1bit_fde_cycle_1_a_plus_1));
  // NotConnected on PCI
  // NotConnected on IFE
endmodule
