// Digital circuit 4Bit_CU_ALU_Master_Mapper.dig as structural Verilog
module _4Bit_CU_ALU_Master_Mapper (
  input  A,
  input  B,
  input  C,
  input  D,
  output [2:0] ALU
);

  ALU_Sub_Mapper_X alu_sub_mapper_x_1 (.A(A), .B(B), .C(C), .D(D), .X(ALU[0]));
  ALU_Sub_Mapper_Y alu_sub_mapper_y_1 (.A(A), .B(B), .C(C), .D(D), .Y(ALU[1]));
  ALU_Sub_Mapper_Z alu_sub_mapper_z_1 (.A(A), .B(B), .C(C), .D(D), .Z(ALU[2]));
endmodule
