// Digital circuit 4Bit_Program_Counter.dig as structural Verilog
module _4Bit_Program_Counter (
  input  Clear,
  input  [3:0] Read,
  input  K,
  input  [3:0] PCin,
  input  CTRL,
  output [3:0] Out
);

  wire [3:0] _4bit_full_adder_1_p4, multiplexer_1_out;

  Multiplexer #(.Bits(4)) multiplexer_1 (
    .sel(CTRL), .in_0(PCin), .in_1(_4bit_full_adder_1_p4), .out(multiplexer_1_out));
  // _4Bit_Register _4bit_register_1: pin names not known; wires that end beside it: multiplexer_1_out, K, Read, Clear, Out
  // _4Bit_Full_Adder _4bit_full_adder_1: pin names not known; wires that end beside it: 4'b0001, Out, 1'b0, _4bit_full_adder_1_p4
endmodule
