// Digital circuit 4Bit_Ram_Module.dig as structural Verilog
module _4Bit_Ram_Module (
  input  K,
  input  [3:0] A,
  input  [3:0] Din,
  output [3:0] Dout
);

  wire and_1_out, and_2_out, and_3_out, and_4_out, and_5_out, and_6_out, and_7_out, and_8_out, and_9_out,
       and_10_out, and_11_out, and_12_out, and_13_out, and_14_out, and_15_out, and_16_out, decoder_1_out_0,
       decoder_1_out_1, decoder_1_out_2, decoder_1_out_3, decoder_1_out_4, decoder_1_out_5, decoder_1_out_6,
       decoder_1_out_7, decoder_1_out_8, decoder_1_out_9, decoder_1_out_10, decoder_1_out_11,
       decoder_1_out_12, decoder_1_out_13, decoder_1_out_14, decoder_1_out_15;
  wire [3:0] d_ff_1_q, d_ff_2_q, d_ff_3_q, d_ff_4_q, d_ff_5_q, d_ff_6_q, d_ff_7_q, d_ff_8_q, d_ff_9_q,
       d_ff_10_q, d_ff_11_q, d_ff_12_q, d_ff_13_q, d_ff_14_q, d_ff_15_q, d_ff_16_q;

  Decoder #(.Selector_Bits(4)) decoder_1 (
    .sel(A), .out_0(decoder_1_out_0), .out_1(decoder_1_out_1), .out_2(decoder_1_out_2),
    .out_3(decoder_1_out_3), .out_4(decoder_1_out_4), .out_5(decoder_1_out_5), .out_6(decoder_1_out_6),
    .out_7(decoder_1_out_7), .out_8(decoder_1_out_8), .out_9(decoder_1_out_9), .out_10(decoder_1_out_10),
    .out_11(decoder_1_out_11), .out_12(decoder_1_out_12), .out_13(decoder_1_out_13),
    .out_14(decoder_1_out_14), .out_15(decoder_1_out_15));
  and and_1 (and_1_out, decoder_1_out_0, K);
  and and_2 (and_2_out, decoder_1_out_1, K);
  and and_3 (and_3_out, decoder_1_out_2, K);
  and and_4 (and_4_out, decoder_1_out_3, K);
  and and_5 (and_5_out, decoder_1_out_4, K);
  and and_6 (and_6_out, decoder_1_out_5, K);
  and and_7 (and_7_out, decoder_1_out_6, K);
  and and_8 (and_8_out, decoder_1_out_7, K);
  and and_9 (and_9_out, decoder_1_out_8, K);
  and and_10 (and_10_out, decoder_1_out_9, K);
  and and_11 (and_11_out, decoder_1_out_10, K);
  and and_12 (and_12_out, decoder_1_out_11, K);
  and and_13 (and_13_out, decoder_1_out_12, K);
  and and_14 (and_14_out, decoder_1_out_13, K);
  and and_15 (and_15_out, decoder_1_out_14, K);
  and and_16 (and_16_out, decoder_1_out_15, K);
  D_FF #(.Bits(4)) d_ff_1 (.D(Din), .C(and_1_out), .Q(d_ff_1_q));  // open: nQ
  D_FF #(.Bits(4)) d_ff_2 (.D(Din), .C(and_2_out), .Q(d_ff_2_q));  // open: nQ
  D_FF #(.Bits(4)) d_ff_3 (.D(Din), .C(and_3_out), .Q(d_ff_3_q));  // open: nQ
  D_FF #(.Bits(4)) d_ff_4 (.D(Din), .C(and_4_out), .Q(d_ff_4_q));  // open: nQ
  D_FF #(.Bits(4)) d_ff_5 (.D(Din), .C(and_5_out), .Q(d_ff_5_q));  // open: nQ
  D_FF #(.Bits(4)) d_ff_6 (.D(Din), .C(and_6_out), .Q(d_ff_6_q));  // open: nQ
  D_FF #(.Bits(4)) d_ff_7 (.D(Din), .C(and_7_out), .Q(d_ff_7_q));  // open: nQ
  D_FF #(.Bits(4)) d_ff_8 (.D(Din), .C(and_8_out), .Q(d_ff_8_q));  // open: nQ
  D_FF #(.Bits(4)) d_ff_9 (.D(Din), .C(and_9_out), .Q(d_ff_9_q));  // open: nQ
  D_FF #(.Bits(4)) d_ff_10 (.D(Din), .C(and_10_out), .Q(d_ff_10_q));  // open: nQ
  D_FF #(.Bits(4)) d_ff_11 (.D(Din), .C(and_11_out), .Q(d_ff_11_q));  // open: nQ
  D_FF #(.Bits(4)) d_ff_12 (.D(Din), .C(and_12_out), .Q(d_ff_12_q));  // open: nQ
  D_FF #(.Bits(4)) d_ff_13 (.D(Din), .C(and_13_out), .Q(d_ff_13_q));  // open: nQ
  D_FF #(.Bits(4)) d_ff_14 (.D(Din), .C(and_14_out), .Q(d_ff_14_q));  // open: nQ
  D_FF #(.Bits(4)) d_ff_15 (.D(Din), .C(and_15_out), .Q(d_ff_15_q));  // open: nQ
  D_FF #(.Bits(4)) d_ff_16 (.D(Din), .C(and_16_out), .Q(d_ff_16_q));  // open: nQ
  Multiplexer #(.Selector_Bits(4), .Bits(4)) multiplexer_1 (
    .sel(A), .in_0(d_ff_1_q), .in_1(d_ff_2_q), .in_2(d_ff_3_q), .in_3(d_ff_4_q), .in_4(d_ff_5_q),
    .in_5(d_ff_6_q), .in_6(d_ff_7_q), .in_7(d_ff_8_q), .in_8(d_ff_9_q), .in_9(d_ff_10_q), .in_10(d_ff_11_q),
    .in_11(d_ff_12_q), .in_12(d_ff_13_q), .in_13(d_ff_14_q), .in_14(d_ff_15_q), .in_15(d_ff_16_q), .out(Dout));
endmodule
