// Digital circuit ADD_Opcode.dig as structural Verilog
module ADD_Opcode (
  input  A,
  input  B,
  input  C,
  input  D,
  output ADD
);

  wire not_1_out, not_2_out;

  not not_1 (not_1_out, B);
  not not_2 (not_2_out, C);
  and and_1 (ADD, A, not_1_out, not_2_out, D);
endmodule
