// Digital circuit ALU_Sub_Mapper_X.dig as structural Verilog
module ALU_Sub_Mapper_X (
  input  A,
  input  B,
  input  C,
  input  D,
  output X
);

  wire and_1_out, and_2_out, not_1_out, not_2_out;

  not not_1 (not_1_out, C);
  not not_2 (not_2_out, D);
  and and_1 (and_1_out, A, B, not_1_out, D);
  and and_2 (and_2_out, A, B, C, not_2_out);
  or or_1 (X, and_1_out, and_2_out);
endmodule
