// Digital circuit ALU_Sub_Mapper_Y.dig as structural Verilog
module ALU_Sub_Mapper_Y (
  input  A,
  input  B,
  input  C,
  input  D,
  output Y
);

  wire and_1_out, and_2_out, not_1_out, not_2_out, not_3_out;

  and and_1 (and_1_out, A, B, not_1_out, not_2_out);
  not not_1 (not_1_out, C);
  not not_2 (not_2_out, D);
  and and_2 (and_2_out, A, not_3_out, C, D);
  not not_3 (not_3_out, B);
  or or_1 (Y, and_1_out, and_2_out);
endmodule
