// Digital circuit ALU_Sub_Mapper_Z.dig as structural Verilog
module ALU_Sub_Mapper_Z (
  input  A,
  input  B,
  input  C,
  input  D,
  output Z
);

  wire and_1_out, and_2_out, not_1_out;

  not not_1 (not_1_out, D);
  and and_1 (and_1_out, A, B, not_1_out);
  and and_2 (and_2_out, A, C, not_1_out);
  or or_1 (Z, and_1_out, and_2_out);
endmodule
