// Digital circuit AND_Opcode.dig as structural Verilog
module AND_Opcode (
  input  A,
  input  B,
  input  C,
  input  D,
  output AND
);

  wire not_1_out;

  not not_1 (not_1_out, B);
  and and_1 (AND, A, not_1_out, C, D);
endmodule
