// Digital circuit IL_Opcode.dig as structural Verilog
module IL_Opcode (
  input  A,
  input  C,
  input  D,
  output IL
);

  wire and_1_out, and_2_out, not_1_out, not_2_out, not_3_out, not_4_out;

  not not_1 (not_1_out, A);
  not not_2 (not_2_out, C);
  not not_3 (not_3_out, A);
  not not_4 (not_4_out, D);
  and and_1 (and_1_out, not_1_out, not_2_out, D);
  and and_2 (and_2_out, not_3_out, C, not_4_out);
  or or_1 (IL, and_1_out, and_2_out);
endmodule
