// Digital circuit OR_Opcode.dig as structural Verilog
module OR_Opcode (
  input  A,
  input  B,
  input  C,
  input  D,
  output OR
);

  wire not_1_out, not_2_out;

  not not_1 (not_1_out, C);
  not not_2 (not_2_out, D);
  and and_1 (OR, A, B, not_1_out, not_2_out);
endmodule
