// Digital circuit RR1_Opcode.dig as structural Verilog
module RR1_Opcode (
  input  A,
  input  B,
  input  C,
  input  D,
  output RR1
);

  wire and_1_out, and_2_out, not_1_out;

  not not_1 (not_1_out, A);
  and and_1 (and_1_out, not_1_out, B);
  and and_2 (and_2_out, C, D);
  and and_3 (RR1, and_1_out, and_2_out);
endmodule
