// Digital circuit RR2_Opcode.dig as structural Verilog
module RR2_Opcode (
  input  A,
  input  B,
  input  C,
  input  D,
  output RR2
);

  wire and_1_out, and_2_out, and_3_out, not_1_out, not_2_out, not_3_out;

  not not_1 (not_1_out, C);
  not not_2 (not_2_out, D);
  not not_3 (not_3_out, B);
  and and_1 (and_1_out, A, B, not_1_out);
  and and_2 (and_2_out, A, C, not_2_out);
  and and_3 (and_3_out, A, not_3_out, D);
  or or_1 (RR2, and_1_out, and_2_out, and_3_out);
endmodule
