// Digital circuit SLT_Opcode.dig as structural Verilog
module SLT_Opcode (
  input  A,
  input  B,
  input  C,
  input  D,
  output SLT
);

  wire not_1_out;

  not not_1 (not_1_out, D);
  and and_1 (SLT, A, B, C, not_1_out);
endmodule
