// Digital circuit WE_Opcode.dig as structural Verilog
module WE_Opcode (
  input  A,
  input  C,
  input  D,
  output WE
);

  wire and_1_out, and_2_out, and_3_out, and_4_out, not_1_out, not_2_out, not_3_out, not_4_out;

  not not_1 (not_1_out, C);
  not not_2 (not_2_out, A);
  not not_3 (not_3_out, A);
  not not_4 (not_4_out, D);
  and and_1 (and_1_out, A, not_1_out);
  and and_2 (and_2_out, not_2_out, D);
  and and_3 (and_3_out, A, C);
  and and_4 (and_4_out, not_3_out, C, not_4_out);
  or or_1 (WE, and_1_out, and_2_out, and_3_out, and_4_out);
endmodule
