// Digital circuit WR_Opcode.dig as structural Verilog
module WR_Opcode (
  input  A,
  input  B,
  input  C,
  input  D,
  output WR
);

  wire and_1_out, and_2_out, not_1_out, not_2_out, not_3_out, not_4_out, not_5_out, not_6_out;

  not not_1 (not_1_out, B);
  not not_2 (not_2_out, C);
  not not_3 (not_3_out, D);
  not not_4 (not_4_out, A);
  not not_5 (not_5_out, B);
  not not_6 (not_6_out, D);
  and and_1 (and_1_out, A, not_1_out, not_2_out, not_3_out);
  and and_2 (and_2_out, not_4_out, not_5_out, C, not_6_out);
  or or_1 (WR, and_1_out, and_2_out);
endmodule
