// Digital circuit XOR_Opcode.dig as structural Verilog
module XOR_Opcode (
  input  A,
  input  B,
  input  C,
  input  D,
  output XOR
);

  wire not_1_out;

  not not_1 (not_1_out, C);
  and and_1 (XOR, A, B, not_1_out, D);
endmodule
